// Digital circuit main.dig as structural Verilog
module main (
  input  clk,
  input  reset,
  input  [7:0] kb_data,
  input  [12:0] disp_read,
  input  kb_en,
  output [31:0] WB_MUX,
  output [31:0] DISP,
  output [23:0] pc_out
);

  wire BANK_SEL, ctrl_bank_en, ctrl_branch_en, ctrl_csel, ctrl_enc, ctrl_flags_we, ctrl_jump_type,
       ctrl_lut_A, ctrl_lut_B, ctrl_mem_rd, ctrl_mem_wr, ctrl_mul_div_en, ctrl_pc_link_WE, ctrl_reg_we,
       HALT_IN, ir_addr_a, ir_addr_b, ir_addr_c, ir_addr_w, ir_offset, mem_rd_out, nflag_A_zero, pc_link,
       reg_c, seq_exec, seq_fetch;
  wire [1:0] ctrl_cycles, ctrl_shift_op, ctrl_sp_out;
  wire [2:0] ctrl_bus_sel, ctrl_pc_cond, ctrl_pc_src, ctrl_wb_sel;
  wire [3:0] ctrl_byte_sel, ctrl_ir_sel;
  wire [8:0] ir_opcode;
  wire [14:0] csr_flags;
  wire [15:0] mul_nxt_enc;
  wire [23:0] IR_ADDR, mem_addr, pc_save, sp_out;
  wire [31:0] alu_out, ir_bus, mem_din, mem_ram_out, reg_a, reg_b, shift_mul_p_enc;

  // alu_control alu_control_1: pin names not known; wires that end beside it: ir_opcode, ctrl_lut_A, ctrl_csel, ctrl_flags_we, ctrl_lut_B, ctrl_shift_op, ctrl_mul_div_en, ctrl_enc
  ir_reg_control ir_reg_control_1 (
    .op(ir_opcode), .ir_imm_sel(ctrl_ir_sel), .wb_sel(ctrl_wb_sel), .reg_we(ctrl_reg_we));
  mem_bus_control mem_bus_control_1 (.op(ir_opcode), .ctrl_bussel(ctrl_bus_sel));
  mem_io_control mem_io_control_1 (
    .op(ir_opcode), .seq_fetch(seq_fetch), .bank_en(ctrl_bank_en), .mem_rd(ctrl_mem_rd),
    .mem_wr(ctrl_mem_wr), .byte_sel(ctrl_byte_sel));
  pc_control pc_control_1 (
    .exec(seq_exec), .op(ir_opcode), .branch_en(ctrl_branch_en), .jump_type(ctrl_jump_type),
    .pc_src(ctrl_pc_src), .pc_link_we(ctrl_pc_link_WE), .cycles(ctrl_cycles), .pc_cond(ctrl_pc_cond),
    .sp_out(ctrl_sp_out), .HALT_IN(HALT_IN));
  // alu_32b_final alu_32b_final_1: pin names not known; wires that end beside it: ctrl_lut_A, ctrl_lut_B, reg_a, ir_bus, reg_c, ctrl_csel, ctrl_flags_we, clk, alu_out, csr_flags
  // register register_1: pin names not known; wires that end beside it: ctrl_reg_we, WB_MUX, ir_addr_a, ir_addr_b, ir_addr_w, seq_exec, clk, BANK_SEL, ctrl_bank_en, ir_addr_c, reg_a, reg_b, reg_c
  mul_div mul_div_1 (
    .B(ir_bus), .mode(ctrl_shift_op), .mul_div(ctrl_mul_div_en), .A(reg_a), .p_enc(ctrl_enc),
    .Out(shift_mul_p_enc), .nflag_A_is_Z(nflag_A_zero), .mul_nxt_enc(mul_nxt_enc));
  vga vga_1 (.mem_addr(mem_addr), .mem_din(WB_MUX), .disp_read_addr(disp_read), .clk(clk), .disp_data_out(DISP));
  // ir ir_1: pin names not known; wires that end beside it: mem_din, seq_fetch, clk, ctrl_ir_sel, reg_b, ir_opcode, ir_addr_a, ir_addr_b, ir_addr_w, IR_ADDR, ir_offset, ir_bus, BANK_SEL, ir_addr_c
  RAMDualPort #(.AddrBits(24), .Bits(32)) ramdualport_1 (
    .A(mem_addr), .Din(WB_MUX), .str(ctrl_mem_wr), .C(clk), .ld(mem_rd_out), .D(mem_ram_out));
  byte_lane_decoder byte_lane_decoder_1 (
    .mem_in(mem_ram_out), .sel_in(ctrl_byte_sel), .io_data_in(kb_data), .mem_out(mem_din));
  // program_counter program_counter_1: pin names not known; wires that end beside it: mem_din, alu_out, ctrl_pc_src, ir_offset, reset, ctrl_cycles, csr_flags, ctrl_pc_cond, ctrl_jump_type, ctrl_branch_en, 1'b1, HALT_IN, kb_en, 1'b1, 1'b1, 1'b1, ctrl_pc_link_WE, clk, pc_out, pc_save, seq_fetch, seq_exec, pc_link
  sp sp_1 (.sp_op(ctrl_sp_out), .CLK(clk), .Reset(reset), .sp_load_in(alu_out), .seq_exec(seq_exec), .sp_out(sp_out));
  wb_mux wb_mux_1 (
    .wb_sel(ctrl_wb_sel), .alu_out(alu_out), .shift_mul(shift_mul_p_enc), .pc_save(pc_save),
    .mem_din(mem_din), .reg_a(reg_a), .ir_bus(ir_bus), .csr_flag(csr_flags), .mul_nxt_enc(mul_nxt_enc),
    .reg_w_data(WB_MUX));
  bus_arbitration bus_arbitration_1 (
    .FETCH(seq_fetch), .IR_ADDR(IR_ADDR), .MEM_RD_IN(ctrl_mem_rd), .addr_sel(ctrl_bus_sel), .Reg_b(reg_b),
    .Pc_out(pc_out), .SP_out(sp_out), .Alu_in(alu_out), .ADDR_BUS(mem_addr), .MEM_RD_OUT(mem_rd_out));

  // Other names for the same wires on the sheet: disp_out[31:0] = DISP; disp_read_addr[12:0] = disp_read;
  //   wb_data[31:0] = WB_MUX

  // Notes on the sheet:
  //   Control Unit
  //   ALU
  //   Shift - Encoder
  //   Memory
  //   Instruction Register
  //   Program Counter
  //   Data Bus Switch
endmodule

/* Test case tomato-v1-burn:
reset pc_out
# tomato.v1 microcode burned into nested control boards
# ascertain hex via: *-control.dig tomato-v1-burn tests
# burn count: 28 opcodes from docs/isa/tomato.v1.csv
# 0x00 NOP system
# 0x01 ADD alu-reg
# 0x02 SUB alu-reg
# 0x03 AND alu-reg
# 0x04 OR alu-reg
# 0x05 XOR alu-reg
# 0x06 MOV alu-reg
# 0x07 CMP alu-reg
# 0x20 ADDI alu-imm
# 0x21 ANDI alu-imm
# 0x22 ORI alu-imm
# 0x23 XORI alu-imm
# 0x24 LUI alu-imm
# 0x40 LSL shift
# 0x41 LSR shift
# 0x42 ASR shift
# 0x60 LW mem
# 0x61 LB mem
# 0x68 SW mem
# 0x69 SB mem
# 0x80 BEQ branch
# 0x81 BNE branch
# 0x82 BLT branch
# 0xA0 JMP jump
# 0xA1 JAL jump
# 0xA2 RET jump
# 0xA3 JR jump
# 0xFF HALT system
1 x
0 x
*/
